# Fritzing sketch timestamper (saved by Fritzing 0.9.6b)
breadboards: 1

parts:
  ENCODER1 = Rotary Encoder with Knob [part_number="Adafruit #377"]
  Part4 = Adafruit QT Py ESP32-S2 [part_number="Adafruit #5325"]
  Part3 = Thermal Printer [part_number="Adafruit #597"]
  Part5 = Adafruit I2C+SPI LCD Backpack [part_number="Adafruit #292"]
  R1 = Resistor [tolerance=±5% power=0.25W resistance=2.2k package=THT]
  R2 = Resistor [tolerance=±5% power=0.25 resistance=3.3k package=THT]

nets:
  N1: ENCODER1.no_name_yet#1, Part4.A2
  N2: ENCODER1.no_name_yet#2, Part4.A3
  GND: ENCODER1.no_name_yet#3, ENCODER1.no_name_yet#5, Part4.GND, Part3.GND, Part5.GND, R2.Pin_1
  N3: ENCODER1.no_name_yet#4, Part4.A1
  N4: Part4.TX, Part3.RXD
  N5: Part4.RX, R1.Pin_1, R2.Pin_0
  N6: Part4.SCK, Part5.CLOCK
  N7: Part4.MISO, Part5.LATCH
  N8: Part4.MOSI, Part5.DATA
  +5V: Part4.+5V, Part3.VH, Part5.VCC
  N9: Part3.TXD, R1.Pin_0

custom parts:
  Rotary Encoder with Knob: Rotary Encoder with 1/4" Shaft and Knob
  Adafruit QT Py ESP32-S2: What has your favorite Espressif WiFi microcontroller, comes with our favorite connector - the STEMMA QT, a chainable I2C port, and has lots of Flash and RAM memory for your next IoT project? What will make your next IoT project flyyyyy? What a cutie pie! Or is it... a QT Py? This diminutive dev board comes with one of our new favorite lil chips, the ESP32-S2! The ESP32-S2 is a highly-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
  Adafruit I2C+SPI LCD Backpack: LCD backpacks reduce the number of pins needed to connect to an LCD. LCDs are a fun and easy way to have your microcontroller project talk back to you. Character LCDs are common, and easy to get, available in tons of colors and sizes. We've written tutorials on using character LCDs with an Arduino (or similar microcontroller) but find that the number of pins necessary to control the LCD can be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
